# Fritzing sketch plotter (saved by Fritzing 1.0.1rc)

parts:
  A1 = Raspberry Pi Pico W
  Pen_up = Pushbutton [package="[THT]"]
  Pen_down = Pushbutton [package="[THT]"]
  M1_up = Pushbutton [package="[THT]"]
  Start = Pushbutton [package="[THT]"]
  M2_down = Pushbutton [package="[THT]"]
  M2_up = Pushbutton [package="[THT]"]
  M1_down = Pushbutton [package="[THT]"]
  Motor_2 = 28BYJ-48 Driver Module [part_number=ULN2003 package=THT]
  Motor_1 = 28BYJ-48 Driver Module [part_number=ULN2003 package=THT]
  SM1 = 28BYJ-48 Stepper Motor [part_number=28BYJ-48]
  SM2 = 28BYJ-48 Stepper Motor [part_number=28BYJ-48]
  Servo_SG90 = Dagu DGServo 9g (Top view) [part_number=RS001B]
  Reset = Pushbutton [package="[SMD]"]

nets:
  N1: A1.pin_1, Motor_2.IN1
  N2: A1.pin_2, Motor_2.IN2
  GND: A1.pin_3, A1.pin_8, A1.pin_13, A1.pin_18, A1.pin_23, A1.pin_28, A1.pin_33, A1.pin_38, Pen_up.Pin_1, Pen_up.Pin_2, Pen_down.Pin_1, Pen_down.Pin_2, M1_up.Pin_1, Start.Pin_1, M2_down.Pin_1, M2_down.Pin_2, M2_up.Pin_1, M2_up.Pin_2, M1_down.Pin_1, M1_down.Pin_2, Motor_2.GND, Motor_1.GND, Servo_SG90.gnd, Reset.Pin_1
  N3: A1.pin_4, Motor_2.IN3
  N4: A1.pin_5, Motor_2.IN4
  N5: A1.pin_9, Motor_1.IN1
  N6: A1.pin_10, Motor_1.IN2
  N7: A1.pin_11, Motor_1.IN3
  N8: A1.pin_12, Motor_1.IN4
  N9: A1.pin_17, Start.Pin_3, Start.Pin_4
  N10: A1.pin_19, Servo_SG90.pulse
  N11: A1.pin_21, Pen_up.Pin_4
  N12: A1.pin_22, Pen_down.Pin_4
  N13: A1.pin_24, M2_down.Pin_4
  N14: A1.pin_25, M2_up.Pin_4
  N15: A1.pin_26, M1_down.Pin_4
  N16: A1.pin_27, M1_up.Pin_4
  N17: A1.pin_30, Reset.Pin_3, Reset.Pin_4
  N18: A1.pin_40, Motor_2.Vmotor, Motor_1.Vmotor, Servo_SG90.vcc
  N19: Motor_2.blue-pin, SM1.blue-pin
  N20: Motor_2.pink-pin, SM1.pink-pin
  N21: Motor_2.yellow-pin, SM1.yellow-pin
  N22: Motor_2.orange-pin, SM1.orange-pin
  N23: Motor_2.red-pin, SM1.red-pin
  N24: Motor_1.blue-pin, SM2.blue-pin
  N25: Motor_1.pink-pin, SM2.pink-pin
  N26: Motor_1.yellow-pin, SM2.yellow-pin
  N27: Motor_1.orange-pin, SM2.orange-pin
  N28: Motor_1.red-pin, SM2.red-pin

custom parts:
  Raspberry Pi Pico W: Raspberry Pi Pico W. Based around the RP2040 microcontroller the Pico W is a low cost microcontroller device bringing Raspberry Pi quality, cost, and easy of use to the microcontroller space. The areas marked KEEPOUT in pcb silkscreen should not have traces running through them to avoid shorts on a soldered in module!
  28BYJ-48 Driver Module: ULN2003 Driver Module for the 28BYJ-48 Unipolar Stepper Motor LED A - Blue wire - Bottom coil left LED B - Pink wire - Top coil left LED C - Yellow wire - Bottom coil right LED D - Orange wire - Top coil right Common rail - red Connector pins: blue - pink - yellow - orange - red Control pins - IN1 to IN4 Power pins - GND & Vmotor (5-12V) On/Off jumper (if removed, power to motor is cut).
  28BYJ-48 Stepper Motor: Unipolar Stepper Motor 28BYJ-48 Top coil - pink & orange Bottom coil - blue & yellow Common rail - red Connector pins: blue - pink - yellow - orange - red
